# Fritzing sketch logger (saved by Fritzing 0.7.5b)
breadboards: 1

parts:
  WeMos_D1_Mini1 = WeMos D1 Mini
  U1 = mystery part, 6 pins [chip_label=BMP280 spacing=300mil]

nets:
  N1: WeMos_D1_Mini1.3V3, U1.pin1, U1.pin5
  N2: WeMos_D1_Mini1.D1, U1.pin3
  N3: WeMos_D1_Mini1.D2, U1.pin4
  N4: WeMos_D1_Mini1.G, U1.pin2, U1.pin6

custom parts:
  WeMos D1 Mini: The D1 mini is a mini wifi board based on ESP-8266EX.
